// Logisim project alu.circ as structural Verilog: 1 circuit, main circuit alu
module alu (
  input  [31:0] A,
  input  [31:0] B,
  input  [3:0] ALUSel,
  output [31:0] ALUResult
);

  wire comparator_1_lt;
  wire [4:0] bit_extender_1_out, bit_extender_2_out, bit_extender_3_out;
  wire [31:0] add0, and0, mul0, mulh0, mulhu0, multiplexer_1_out, multiplexer_2_out, multiplexer_3_out,
       multiplexer_4_out, multiplexer_5_out, multiplexer_6_out, multiplexer_7_out, multiplexer_8_out,
       multiplexer_9_out, multiplexer_10_out, multiplexer_11_out, multiplexer_12_out, multiplexer_13_out,
       multiplexer_14_out, or0, sll0, slt0, sra0, srl0, sub0, undriven, undriven_2, undriven_3, xor0;

  Bit_Extender #(.in_width(32), .out_width(5), .\type ("zero")) bit_extender_1 (.in(B), .out(bit_extender_1_out));
  Bit_Extender #(.in_width(32), .out_width(5), .\type ("zero")) bit_extender_2 (.in(B), .out(bit_extender_2_out));
  Bit_Extender #(.in_width(32), .out_width(5), .\type ("zero")) bit_extender_3 (.in(B), .out(bit_extender_3_out));
  Comparator #(.width(32)) comparator_1 (.a(A), .b(B), .lt(comparator_1_lt));  // open: gt, eq
  Shifter #(.shift("lr"), .width(32)) shifter_1 (.in(A), .\dist (bit_extender_2_out), .out(srl0));
  Shifter #(.shift("ar"), .width(32)) shifter_2 (.in(A), .\dist (bit_extender_3_out), .out(sra0));
  Subtractor #(.width(32)) subtractor_1 (.a(A), .b(B), .out(sub0));  // open: bin, bout
  assign xor0 = A ^ B;  // XOR_Gate xor_1, 32 bits wide
  assign or0 = A | B;  // OR_Gate or_1, 32 bits wide
  assign and0 = A & B;  // AND_Gate and_1, 32 bits wide
  Multiplier #(.mode("twosComplement"), .width(32)) multiplier_1 (.a(A), .b(B), .out(mul0), .cout(mulh0));  // open: cin
  Multiplier #(.width(32)) multiplier_2 (.a(A), .b(B), .cout(mulhu0));  // open: out, cin
  Adder #(.width(32)) adder_1 (.a(A), .b(B), .out(add0));  // open: cin, cout
  Shifter #(.width(32)) shifter_3 (.in(A), .\dist (bit_extender_1_out), .out(sll0));
  assign slt0 = {{31{1'b0}}, comparator_1_lt};  // Bit_Extender bit_extender_4
  Multiplexer #(.width(32)) multiplexer_1 (.in0(add0), .in1(sll0), .out(multiplexer_1_out), .sel(ALUSel[0]));
  Multiplexer #(.width(32)) multiplexer_2 (.in0(slt0), .in1(undriven_3), .out(multiplexer_2_out), .sel(ALUSel[0]));
  Multiplexer #(.width(32)) multiplexer_3 (.in0(xor0), .in1(srl0), .out(multiplexer_3_out), .sel(ALUSel[0]));
  Multiplexer #(.width(32)) multiplexer_4 (.in0(or0), .in1(and0), .out(multiplexer_4_out), .sel(ALUSel[0]));
  Multiplexer #(.width(32)) multiplexer_5 (.in0(mul0), .in1(mulh0), .out(multiplexer_5_out), .sel(ALUSel[0]));
  Multiplexer #(.width(32)) multiplexer_6 (.in0(undriven_2), .in1(mulhu0), .out(multiplexer_6_out), .sel(ALUSel[0]));
  Multiplexer #(.width(32)) multiplexer_7 (.in0(sub0), .in1(sra0), .out(multiplexer_7_out), .sel(ALUSel[0]));
  Multiplexer #(.width(32)) multiplexer_8 (.in0(undriven), .in1(B), .out(multiplexer_8_out), .sel(ALUSel[0]));
  Multiplexer #(.width(32)) multiplexer_9 (
    .in0(multiplexer_1_out), .in1(multiplexer_2_out), .out(multiplexer_9_out), .sel(ALUSel[1]));
  Multiplexer #(.width(32)) multiplexer_10 (
    .in0(multiplexer_3_out), .in1(multiplexer_4_out), .out(multiplexer_10_out), .sel(ALUSel[1]));
  Multiplexer #(.width(32)) multiplexer_11 (
    .in0(multiplexer_5_out), .in1(multiplexer_6_out), .out(multiplexer_11_out), .sel(ALUSel[1]));
  Multiplexer #(.width(32)) multiplexer_12 (
    .in0(multiplexer_7_out), .in1(multiplexer_8_out), .out(multiplexer_12_out), .sel(ALUSel[1]));
  Multiplexer #(.width(32)) multiplexer_13 (
    .in0(multiplexer_9_out), .in1(multiplexer_10_out), .out(multiplexer_13_out), .sel(ALUSel[2]));
  Multiplexer #(.width(32)) multiplexer_14 (
    .in0(multiplexer_11_out), .in1(multiplexer_12_out), .out(multiplexer_14_out), .sel(ALUSel[2]));
  Multiplexer #(.width(32)) multiplexer_15 (
    .in0(multiplexer_13_out), .in1(multiplexer_14_out), .out(ALUResult), .sel(ALUSel[3]));

  // Notes on the sheet:
  //   INPUTS to your circuit
  //   DON'T CHANGE THE LOCATIONS OF THE INPUTS AND OUTPUTS!
  //   OUTPUT from your circuit
endmodule
