// Logisim project control-logic.circ as structural Verilog: 1 circuit, main circuit control_logic
module control_logic (
  input  [31:0] Instruction,
  input  BrEq,
  input  BrLt,
  output PCSel,
  output RegWEn,
  output [2:0] ImmSel,
  output BrUn,
  output ASel,
  output BSel,
  output [3:0] ALUSel,
  output MemWEn,
  output [1:0] WBSel
);

  wire Add0, Addi0, And0, and_1_out, and_2_out, and_3_out, and_4_out, and_5_out, and_6_out, and_7_out,
       and_8_out, Andi0, Auipc0, Beq0, Bge0, Bgeu0, Blt0, Bltu0, Bne0, comparator_37_eq, comparator_38_eq,
       comparator_39_eq, comparator_40_eq, Jal0, Jalr0, Lb0, Lh0, Lui0, Lw0, Mul0, Mulh0, Mulhu0,
       multiplexer_1_out, not_1_out, not_2_out, not_3_out, not_4_out, not_5_out, Or0, or_1_out, Ori0, Sb0,
       Sh0, Sll0, Slli0, Slt0, Slti0, Sra0, Srai0, Srl0, Srli0, Sub0, Sw0, Xor0, Xori0;
  wire [4:0] bit_extender_1_out, bit_extender_2_out, bit_extender_3_out, bit_extender_4_out,
       bit_extender_23_out_2;
  wire [4:3] bit_extender_23_out;
  wire [5:0] ROMinputs;
  wire [6:0] bit_extender_22_out;
  wire [7:0] bit_extender_5_out, bit_extender_6_out, bit_extender_7_out, bit_extender_8_out,
       bit_extender_9_out, bit_extender_10_out, bit_extender_11_out, bit_extender_12_out,
       bit_extender_13_out, bit_extender_14_out, bit_extender_15_out, bit_extender_16_out,
       bit_extender_17_out, bit_extender_18_out, bit_extender_19_out, bit_extender_20_out,
       bit_extender_21_out;
  wire [15:0] rom_1_data;

  // Probe on Instruction[6:2]
  not not_1 (not_1_out, BrLt);
  // Probe on {Instruction[31:25], Instruction[14:12], Instruction[6:2]}
  // Probe on {Instruction[31:25], Instruction[14:12], Instruction[6:2]}
  not not_2 (not_2_out, BrEq);
  not not_3 (not_3_out, BrLt);
  not not_4 (not_4_out, BrEq);
  and and_1 (and_1_out, not_4_out, not_1_out);
  // Probe on {Instruction[31:25], Instruction[14:12], Instruction[6:2]}
  Bit_Extender #(.in_width(15), .out_width(5), .\type ("zero")) bit_extender_1 (
    .in({Instruction[31:25], Instruction[14:12], Instruction[6:2]}), .out(bit_extender_1_out));
  Bit_Extender #(.in_width(15), .out_width(5), .\type ("zero")) bit_extender_2 (
    .in({Instruction[31:25], Instruction[14:12], Instruction[6:2]}), .out(bit_extender_2_out));
  Bit_Extender #(.in_width(15), .out_width(5), .\type ("zero")) bit_extender_3 (
    .in({Instruction[31:25], Instruction[14:12], Instruction[6:2]}), .out(bit_extender_3_out));
  Bit_Extender #(.in_width(15), .out_width(5), .\type ("zero")) bit_extender_4 (
    .in({Instruction[31:25], Instruction[14:12], Instruction[6:2]}), .out(bit_extender_4_out));
  // Probe on Instruction[14:12]
  // Probe on Instruction[31:25]
  Bit_Extender #(.in_width(15), .out_width(8), .\type ("zero")) bit_extender_5 (
    .in({Instruction[31:25], Instruction[14:12], Instruction[6:2]}), .out(bit_extender_5_out));
  Bit_Extender #(.in_width(15), .out_width(8), .\type ("zero")) bit_extender_6 (
    .in({Instruction[31:25], Instruction[14:12], Instruction[6:2]}), .out(bit_extender_6_out));
  Bit_Extender #(.in_width(15), .out_width(8), .\type ("zero")) bit_extender_7 (
    .in({Instruction[31:25], Instruction[14:12], Instruction[6:2]}), .out(bit_extender_7_out));
  Bit_Extender #(.in_width(15), .out_width(8), .\type ("zero")) bit_extender_8 (
    .in({Instruction[31:25], Instruction[14:12], Instruction[6:2]}), .out(bit_extender_8_out));
  Bit_Extender #(.in_width(15), .out_width(8), .\type ("zero")) bit_extender_9 (
    .in({Instruction[31:25], Instruction[14:12], Instruction[6:2]}), .out(bit_extender_9_out));
  // Probe on bit_extender_10_out
  Bit_Extender #(.in_width(15), .out_width(8), .\type ("zero")) bit_extender_10 (
    .in({Instruction[31:25], Instruction[14:12], Instruction[6:2]}), .out(bit_extender_10_out));
  Bit_Extender #(.in_width(15), .out_width(8), .\type ("zero")) bit_extender_11 (
    .in({Instruction[31:25], Instruction[14:12], Instruction[6:2]}), .out(bit_extender_11_out));
  Bit_Extender #(.in_width(15), .out_width(8), .\type ("zero")) bit_extender_12 (
    .in({Instruction[31:25], Instruction[14:12], Instruction[6:2]}), .out(bit_extender_12_out));
  Bit_Extender #(.in_width(15), .out_width(8), .\type ("zero")) bit_extender_13 (
    .in({Instruction[31:25], Instruction[14:12], Instruction[6:2]}), .out(bit_extender_13_out));
  Bit_Extender #(.in_width(15), .out_width(8), .\type ("zero")) bit_extender_14 (
    .in({Instruction[31:25], Instruction[14:12], Instruction[6:2]}), .out(bit_extender_14_out));
  Bit_Extender #(.in_width(15), .out_width(8), .\type ("zero")) bit_extender_15 (
    .in({Instruction[31:25], Instruction[14:12], Instruction[6:2]}), .out(bit_extender_15_out));
  and and_2 (and_2_out, not_2_out, not_3_out);
  // Probe on bit_extender_16_out
  Bit_Extender #(.in_width(15), .out_width(8), .\type ("zero")) bit_extender_16 (
    .in({Instruction[31:25], Instruction[14:12], Instruction[6:2]}), .out(bit_extender_16_out));
  Bit_Extender #(.in_width(15), .out_width(8), .\type ("zero")) bit_extender_17 (
    .in({Instruction[31:25], Instruction[14:12], Instruction[6:2]}), .out(bit_extender_17_out));
  Bit_Extender #(.in_width(15), .out_width(8), .\type ("zero")) bit_extender_18 (
    .in({Instruction[31:25], Instruction[14:12], Instruction[6:2]}), .out(bit_extender_18_out));
  Bit_Extender #(.in_width(15), .out_width(8), .\type ("zero")) bit_extender_19 (
    .in({Instruction[31:25], Instruction[14:12], Instruction[6:2]}), .out(bit_extender_19_out));
  Bit_Extender #(.in_width(15), .out_width(8), .\type ("zero")) bit_extender_20 (
    .in({Instruction[31:25], Instruction[14:12], Instruction[6:2]}), .out(bit_extender_20_out));
  Bit_Extender #(.in_width(15), .out_width(8), .\type ("zero")) bit_extender_21 (
    .in({Instruction[31:25], Instruction[14:12], Instruction[6:2]}), .out(bit_extender_21_out));
  // Probe on bit_extender_1_out
  // Probe on bit_extender_3_out
  // Probe on {Instruction[31:25], Instruction[14:12], Instruction[6:2]}
  Comparator #(.mode("unsigned")) comparator_1 (.a(bit_extender_5_out), .b(8'h4), .eq(Addi0));  // open: gt, lt
  Comparator #(.width(15)) comparator_2 (
    .a({Instruction[31:25], Instruction[14:12], Instruction[6:2]}), .b(15'h24), .eq(Slli0));  // open: gt, lt
  Comparator comparator_3 (.a(bit_extender_6_out), .b(8'h44), .eq(Slti0));  // open: gt, lt
  Comparator comparator_4 (.a(bit_extender_7_out), .b(8'h84), .eq(Xori0));  // open: gt, lt
  Comparator #(.width(15)) comparator_5 (
    .a({Instruction[31:25], Instruction[14:12], Instruction[6:2]}), .b(15'ha4), .eq(Srli0));  // open: gt, lt
  Comparator #(.width(15)) comparator_6 (
    .a({Instruction[31:25], Instruction[14:12], Instruction[6:2]}), .b(15'h20a4), .eq(Srai0));  // open: gt, lt
  Comparator comparator_7 (.a(bit_extender_8_out), .b(8'hc4), .eq(Ori0));  // open: gt, lt
  Comparator comparator_8 (.a(bit_extender_9_out), .b(8'he4), .eq(Andi0));  // open: gt, lt
  Comparator #(.width(15)) comparator_9 (
    .a({Instruction[31:25], Instruction[14:12], Instruction[6:2]}), .b(15'hc), .eq(Add0));  // open: gt, lt
  Comparator #(.width(15)) comparator_10 (
    .a({Instruction[31:25], Instruction[14:12], Instruction[6:2]}), .b(15'h10c), .eq(Mul0));  // open: gt, lt
  Comparator #(.width(15)) comparator_11 (
    .a({Instruction[31:25], Instruction[14:12], Instruction[6:2]}), .b(15'h200c), .eq(Sub0));  // open: gt, lt
  Comparator #(.width(15)) comparator_12 (
    .a({Instruction[31:25], Instruction[14:12], Instruction[6:2]}), .b(15'h2c), .eq(Sll0));  // open: gt, lt
  Comparator #(.width(15)) comparator_13 (
    .a({Instruction[31:25], Instruction[14:12], Instruction[6:2]}), .b(15'h12c), .eq(Mulh0));  // open: gt, lt
  Comparator #(.width(15)) comparator_14 (
    .a({Instruction[31:25], Instruction[14:12], Instruction[6:2]}), .b(15'h16c), .eq(Mulhu0));  // open: gt, lt
  Comparator #(.width(15)) comparator_15 (
    .a({Instruction[31:25], Instruction[14:12], Instruction[6:2]}), .b(15'h4c), .eq(Slt0));  // open: gt, lt
  Comparator #(.width(15)) comparator_16 (
    .a({Instruction[31:25], Instruction[14:12], Instruction[6:2]}), .b(15'h8c), .eq(Xor0));  // open: gt, lt
  Comparator #(.width(15)) comparator_17 (
    .a({Instruction[31:25], Instruction[14:12], Instruction[6:2]}), .b(15'hac), .eq(Srl0));  // open: gt, lt
  Comparator #(.width(15)) comparator_18 (
    .a({Instruction[31:25], Instruction[14:12], Instruction[6:2]}), .b(15'h20ac), .eq(Sra0));  // open: gt, lt
  Comparator #(.width(15)) comparator_19 (
    .a({Instruction[31:25], Instruction[14:12], Instruction[6:2]}), .b(15'hcc), .eq(Or0));  // open: gt, lt
  Comparator #(.width(15)) comparator_20 (
    .a({Instruction[31:25], Instruction[14:12], Instruction[6:2]}), .b(15'hec), .eq(And0));  // open: gt, lt
  Comparator comparator_21 (.a(bit_extender_10_out), .b(8'h18), .eq(Beq0));  // open: gt, lt
  Comparator comparator_22 (.a(bit_extender_11_out), .b(8'h38), .eq(Bne0));  // open: gt, lt
  Comparator comparator_23 (.a(bit_extender_12_out), .b(8'h98), .eq(Blt0));  // open: gt, lt
  Comparator comparator_24 (.a(bit_extender_13_out), .b(8'hb8), .eq(Bge0));  // open: gt, lt
  Comparator comparator_25 (.a(bit_extender_14_out), .b(8'hd8), .eq(Bltu0));  // open: gt, lt
  Comparator comparator_26 (.a(bit_extender_15_out), .b(8'hf8), .eq(Bgeu0));  // open: gt, lt
  not not_5 (not_5_out, BrEq);
  // NoConnect on nothing
  Comparator comparator_27 (.a(bit_extender_16_out), .b({8{1'b0}}), .eq(Lb0));  // open: gt, lt
  Comparator comparator_28 (.a(bit_extender_17_out), .b(8'h20), .eq(Lh0));  // open: gt, lt
  Comparator comparator_29 (.a(bit_extender_18_out), .b(8'h40), .eq(Lw0));  // open: gt, lt
  Comparator comparator_30 (.a(bit_extender_19_out), .b(8'h8), .eq(Sb0));  // open: gt, lt
  Comparator comparator_31 (.a(bit_extender_20_out), .b(8'h28), .eq(Sh0));  // open: gt, lt
  Comparator comparator_32 (.a(bit_extender_21_out), .b(8'h48), .eq(Sw0));  // open: gt, lt
  Comparator #(.width(5)) comparator_33 (.a(bit_extender_1_out), .b(5'b00101), .eq(Auipc0));  // open: gt, lt
  Comparator #(.width(5)) comparator_34 (.a(bit_extender_2_out), .b(5'b01101), .eq(Lui0));  // open: gt, lt
  Comparator #(.width(5)) comparator_35 (.a(bit_extender_3_out), .b(5'b11011), .eq(Jal0));  // open: gt, lt
  Comparator #(.width(5)) comparator_36 (.a(bit_extender_4_out), .b(5'b11001), .eq(Jalr0));  // open: gt, lt
  and and_3 (and_3_out, Beq0, BrEq);
  and and_4 (and_4_out, Bne0, not_5_out);
  and and_5 (and_5_out, Blt0, BrLt);
  and and_6 (and_6_out, Bge0, and_2_out);
  and and_7 (and_7_out, Bltu0, BrLt);
  and and_8 (and_8_out, Bgeu0, and_1_out);
  ROM #(.addrWidth(6), .dataWidth(16)) rom_1 (
    .addr(ROMinputs),
    .data({rom_1_data[15:14], WBSel, MemWEn, ALUSel, rom_1_data[6], ASel, BrUn, ImmSel, rom_1_data[0]}));
  or or_1 (or_1_out, and_3_out, and_4_out, and_5_out, and_6_out, and_7_out, and_8_out);
  Bit_Extender #(.in_width(32), .out_width(7), .\type ("zero")) bit_extender_22 (
    .in(Instruction), .out(bit_extender_22_out));
  Bit_Extender #(.in_width(32), .out_width(7), .\type ("zero")) bit_extender_23 (
    .in(Instruction), .out({bit_extender_23_out_2[4:3], bit_extender_23_out, bit_extender_23_out_2[2:0]}));
  Comparator #(.width(7)) comparator_37 (
    .a(bit_extender_22_out), .b(7'b1100011), .eq(comparator_37_eq));  // open: gt, lt
  Priority_Encoder #(.select_enc(6)) priority_encoder_1 (
    .in0(Add0), .in1(Mul0), .in2(Sub0), .in3(Sll0), .in4(Mulh0), .in5(Mulhu0), .in6(Slt0), .in7(Xor0),
    .in8(Srl0), .in9(Sra0), .in10(Or0), .in11(And0), .in12(Lb0), .in13(Lh0), .in14(Lw0), .in15(Addi0),
    .in16(Slli0), .in17(Slti0), .in18(Xori0), .in19(Srli0), .in20(Srai0), .in21(Ori0), .in22(Andi0),
    .in23(Sb0), .in24(Sh0), .in25(Sw0), .in26(Beq0), .in27(Bne0), .in28(Blt0), .in29(Bge0), .in30(Bltu0),
    .in31(Bgeu0), .in32(Auipc0), .in33(Lui0), .in34(Jal0), .in35(Jalr0), .out(ROMinputs));  // open: in36, in37, in38, in39, in40, in41, in42, in43, in44, in45, in46, in47, in48, in49, in50, in51, in52, in53, in54, in55, in56, in57, in58, in59, in60, in61, in62, in63, gs, en_out, en_in
  Comparator #(.width(5)) comparator_38 (
    .a(bit_extender_23_out_2), .b({5{1'b1}}), .eq(comparator_38_eq));  // open: gt, lt
  Multiplexer multiplexer_1 (.in0(1'b0), .in1(1'b1), .out(multiplexer_1_out), .sel(comparator_38_eq));
  Comparator #(.width(32)) comparator_39 (.a(Instruction), .b({32{1'b0}}), .eq(comparator_39_eq));  // open: gt, lt
  Comparator #(.width(32)) comparator_40 (.a(Instruction), .b({32{1'b0}}), .eq(comparator_40_eq));  // open: gt, lt
  Multiplexer multiplexer_2 (.in0(rom_1_data[6]), .in1(1'b0), .out(BSel), .sel(comparator_39_eq));
  Multiplexer multiplexer_3 (.in0(multiplexer_1_out), .in1(or_1_out), .out(PCSel), .sel(comparator_37_eq));
  Multiplexer multiplexer_4 (.in0(rom_1_data[0]), .in1(1'b0), .out(RegWEn), .sel(comparator_40_eq));

  // Other names for the same wires on the sheet: EffectiveInstruction[14:0] = {Instruction[31:25], Instruction[14:12], Instruction[6:2]};
  //   OpCode[4:0] = Instruction[6:2]; Func3[2:0] = Instruction[14:12]; Func7[6:0] = Instruction[31:25]

  // Notes on the sheet:
  //   INPUTS to your circuit
  //   DON'T CHANGE THE LOCATIONS OF THE INPUTS AND OUTPUTS!
  //   OUTPUT from your circuit
  //   contents of rom_1 (hex, n*v repeats v):
  //   1001 1401 1601 1081 1481 1581 1101 1201 1281 1681 1301 1381 41 41 41 1041 10c1 1141 1241 12c1 16c1
  //   1341 13c1 842 842 842 4*1064 1074 1074 1077 17f7 2079 2051
  //   ROM FOR CONTROL LOGIC
  //   This is only if you choose to do the ROM option
  //   CONNECT
  //   WIRE
  //   TO
  //   USE
  //   ROM
  //   Reminder: If using ROM, use combinational logic for PCSel
endmodule
