// Logisim project cpu.circ as structural Verilog: 1 circuit, main circuit cpu
module cpu (
  input  clk,
  input  [31:0] Instruction,
  input  [31:0] MemReadData,
  output [31:0] MemAddress,
  output [31:0] ProgramCounter,
  output [31:0] ra,
  output [31:0] sp,
  output [31:0] t0,
  output [31:0] t1,
  output [31:0] t2,
  output [31:0] s0,
  output [31:0] s1,
  output [31:0] a0,
  output [3:0] MemWriteMask,
  output [31:0] MemWriteData
);

  wire and_1_out, and_2_out, and_3_out, and_4_out, and_5_out, ASel0, BrEq, BrLt, BrUn0, BSel0,
       comparator_1_eq, comparator_2_eq, comparator_3_eq, comparator_4_eq, comparator_5_eq, comparator_6_eq,
       comparator_7_eq, comparator_8_eq, comparator_9_eq, comparator_10_eq, comparator_11_eq, MemWEn0,
       not_1_out, not_2_out, not_3_out, or_1_out, PCSel0, RW0;
  wire [1:0] ForwardSelA, ForwardSelB, ForwardSelSW, WBSel0;
  wire [2:0] ImmSel0;
  wire [3:0] ALUsel0;
  wire [31:0] adder_2_out, ALUResult, bit_extender_1_out, bit_extender_2_out, bit_extender_3_out,
       DataAStage3, DataBStage3, DataBStage4, Immediate, InstStage2, multiplexer_1_out, multiplexer_2_out,
       multiplexer_3_out, multiplexer_6_out, multiplexer_7_out, multiplexer_8_out, multiplexer_9_out,
       multiplexer_10_out, multiplexer_11_out, multiplexer_12_out, partial_load_1_datatoreg, PCPlus4,
       PCStage2, PCStage3, PCStage4, ReadData1, ReadData2, regfile_1_readdata1, regfile_1_readdata2,
       WriteData0, WriteDataStage5;
  wire [45:0] ExInstStage3, ExInstStage4, ExInstStage5;

  Comparator #(.width(5)) comparator_1 (
    .a(InstStage2[11:7]), .b(Instruction[19:15]), .eq(comparator_1_eq));  // open: gt, lt
  Comparator #(.width(5)) comparator_2 (
    .a(InstStage2[11:7]), .b(Instruction[24:20]), .eq(comparator_2_eq));  // open: gt, lt
  Adder #(.width(32)) adder_1 (.a(ProgramCounter), .b(32'h4), .out(PCPlus4));  // open: cin, cout
  Multiplexer #(.width(32)) multiplexer_1 (.in0(PCPlus4), .in1(ALUResult), .out(multiplexer_1_out), .sel(PCSel0));
  Comparator #(.width(7)) comparator_3 (.a(InstStage2[6:0]), .b(7'b0000011), .eq(comparator_3_eq));  // open: gt, lt
  // Probe on Instruction
  or or_1 (or_1_out, comparator_1_eq, comparator_2_eq);
  Multiplexer #(.width(32)) multiplexer_2 (
    .in0(multiplexer_1_out), .in1(ProgramCounter), .out(multiplexer_2_out), .sel(and_1_out));
  and and_1 (and_1_out, comparator_3_eq, or_1_out);
  Register #(.width(32)) PC (.D(multiplexer_2_out), .clk(clk), .Q(ProgramCounter));  // open: en, clr
  Multiplexer #(.width(32)) multiplexer_3 (.in0(Instruction), .in1(32'h13), .out(multiplexer_3_out), .sel(and_1_out));
  Register #(.width(32)) instID (.D(multiplexer_3_out), .en(1'b1), .clk(clk), .Q(InstStage2));  // open: clr
  Register #(.width(32)) pcID (.D(ProgramCounter), .en(1'b1), .clk(clk), .Q(PCStage2));  // open: clr
  control_logic control_logic_1 (
    .Instruction(InstStage2), .BrEq(BrEq), .BrLt(BrLt), .PCSel(PCSel0), .RegWEn(RW0), .ImmSel(ImmSel0),
    .BrUn(BrUn0), .ASel(ASel0), .BSel(BSel0), .ALUSel(ALUsel0), .MemWEn(MemWEn0), .WBSel(WBSel0));
  regfile regfile_1 (
    .ReadIndex1(InstStage2[19:15]), .ReadIndex2(InstStage2[24:20]), .WriteIndex(ExInstStage5[11:7]),
    .WriteData(WriteDataStage5), .RegWEn(ExInstStage5[33]), .clk(clk), .ra(ra), .sp(sp), .t0(t0), .t1(t1),
    .t2(t2), .s0(s0), .s1(s1), .a0(a0), .ReadData1(regfile_1_readdata1), .ReadData2(regfile_1_readdata2));
  Comparator #(.width(5)) comparator_4 (
    .a(InstStage2[19:15]), .b(ExInstStage5[11:7]), .eq(comparator_4_eq));  // open: gt, lt
  not not_1 (not_1_out, comparator_5_eq);
  Comparator #(.width(5)) comparator_5 (.a({5{1'b0}}), .b(ExInstStage5[11:7]), .eq(comparator_5_eq));  // open: gt, lt
  Comparator #(.width(5)) comparator_6 (
    .a(InstStage2[24:20]), .b(ExInstStage5[11:7]), .eq(comparator_6_eq));  // open: gt, lt
  not not_2 (not_2_out, comparator_7_eq);
  Comparator #(.width(5)) comparator_7 (.a({5{1'b0}}), .b(ExInstStage5[11:7]), .eq(comparator_7_eq));  // open: gt, lt
  and and_2 (and_2_out, comparator_4_eq, not_1_out);
  and and_3 (and_3_out, comparator_6_eq, not_2_out);
  Multiplexer #(.width(32)) multiplexer_4 (
    .in0(regfile_1_readdata1), .in1(WriteDataStage5), .out(ReadData1), .sel(and_2_out));
  Multiplexer #(.width(32)) multiplexer_5 (
    .in0(regfile_1_readdata2), .in1(WriteDataStage5), .out(ReadData2), .sel(and_3_out));
  Register #(.width(32)) pcEX (.D(PCStage2), .en(1'b1), .clk(clk), .Q(PCStage3));  // open: clr
  Register #(.width(32)) rs1EX (.D(ReadData1), .en(1'b1), .clk(clk), .Q(DataAStage3));  // open: clr
  Register #(.width(32)) rs2EX (.D(ReadData2), .en(1'b1), .clk(clk), .Q(DataBStage3));  // open: clr
  Register #(.width(46)) register_1 (
    .D({WBSel0, MemWEn0, ALUsel0, BSel0, ASel0, ImmSel0, RW0, PCSel0, InstStage2}), .en(1'b1), .clk(clk),
    .Q(ExInstStage3));  // open: clr
  Multiplexer #(.width(32)) multiplexer_6 (
    .in0(DataBStage3), .in1(Immediate), .out(multiplexer_6_out), .sel(ExInstStage3[38]));
  Comparator #(.width(5)) comparator_8 (
    .a(ExInstStage5[11:7]), .b(ExInstStage3[19:15]), .eq(comparator_8_eq));  // open: gt, lt
  Multiplexer #(.select(2), .width(32)) multiplexer_7 (
    .in0(MemAddress), .in1(WriteDataStage5), .in2(multiplexer_6_out), .out(multiplexer_7_out),
    .sel(ForwardSelB));  // open: in3
  Comparator #(.width(7)) comparator_9 (.a(ExInstStage5[6:0]), .b(7'b0000011), .eq(comparator_9_eq));  // open: gt, lt
  Comparator #(.width(5)) comparator_10 (
    .a(ExInstStage5[11:7]), .b(ExInstStage3[24:20]), .eq(comparator_10_eq));  // open: gt, lt
  Bit_Extender #(.in_width(46), .out_width(32), .\type ("zero")) bit_extender_1 (
    .in(ExInstStage3), .out(bit_extender_1_out));
  Comparator #(.width(7)) comparator_11 (.a(ExInstStage5[6:0]), .b(7'b0000011), .eq(comparator_11_eq));  // open: gt, lt
  Multiplexer #(.width(32)) multiplexer_8 (
    .in0(DataAStage3), .in1(PCStage3), .out(multiplexer_8_out), .sel(ExInstStage3[37]));
  and and_4 (and_4_out, comparator_9_eq, comparator_10_eq);
  and and_5 (and_5_out, comparator_11_eq, comparator_8_eq);
  not not_3 (not_3_out, and_5_out);
  Multiplexer #(.width(32)) multiplexer_9 (
    .in0(WriteDataStage5), .in1(multiplexer_10_out), .out(multiplexer_9_out), .sel(not_3_out));
  Multiplexer #(.select(2), .width(32)) multiplexer_10 (
    .in0(MemAddress), .in1(WriteDataStage5), .in2(multiplexer_8_out), .out(multiplexer_10_out),
    .sel(ForwardSelA));  // open: in3
  Multiplexer #(.width(32)) multiplexer_11 (
    .in0(multiplexer_7_out), .in1(WriteDataStage5), .out(multiplexer_11_out), .sel(and_4_out));
  alu alu_1 (.A(multiplexer_9_out), .B(multiplexer_11_out), .ALUSel(ExInstStage3[42:39]), .ALUResult(ALUResult));
  branch_comp branch_comp_1 (.BrData1(DataAStage3), .BrData2(DataBStage3), .BrUn(BrUn0), .BrEq(BrEq), .BrLt(BrLt));
  imm_gen imm_gen_1 (.Instruction(bit_extender_1_out), .ImmSel(ExInstStage3[36:34]), .Immediate(Immediate));
  forwarding_control_logic forwarding_control_logic_1 (
    .instALU(ExInstStage3), .instMA(ExInstStage4), .instWB(ExInstStage5), .ForwardSelA(ForwardSelA),
    .ForwardSelB(ForwardSelB), .ForwardSelSW(ForwardSelSW));
  Register #(.width(32)) pcMA (.D(PCStage3), .en(1'b1), .clk(clk), .Q(PCStage4));  // open: clr
  Register #(.width(32)) register_2 (.D(ALUResult), .en(1'b1), .clk(clk), .Q(MemAddress));  // open: clr
  Multiplexer #(.select(2), .width(32)) multiplexer_12 (
    .in0(MemAddress), .in1(WriteDataStage5), .in2(DataBStage3), .out(multiplexer_12_out), .sel(ForwardSelSW));  // open: in3
  Register #(.width(46)) register_3 (.D(ExInstStage3), .en(1'b1), .clk(clk), .Q(ExInstStage4));  // open: clr
  Register #(.width(32)) register_4 (.D(multiplexer_12_out), .en(1'b1), .clk(clk), .Q(DataBStage4));  // open: clr
  Bit_Extender #(.in_width(46), .out_width(32), .\type ("zero")) bit_extender_2 (
    .in(ExInstStage4), .out(bit_extender_2_out));
  Bit_Extender #(.in_width(46), .out_width(32), .\type ("zero")) bit_extender_3 (
    .in(ExInstStage4), .out(bit_extender_3_out));
  Adder #(.width(32)) adder_2 (.a(PCStage4), .b(32'h4), .out(adder_2_out));  // open: cin, cout
  partial_store partial_store_1 (
    .Instruction(bit_extender_2_out), .MemAddress(MemAddress), .DataFromReg(DataBStage4),
    .MemWEn(ExInstStage4[43]), .MemWriteMask(MemWriteMask), .DataToMem(MemWriteData));
  partial_load partial_load_1 (
    .Instruction(bit_extender_3_out), .MemAddress(MemAddress), .DataFromMem(MemReadData),
    .DataToReg(partial_load_1_datatoreg));
  Multiplexer #(.select(2), .width(32)) multiplexer_13 (
    .in0(partial_load_1_datatoreg), .in1(MemAddress), .in2(adder_2_out), .out(WriteData0),
    .sel(ExInstStage4[45:44]));  // open: in3
  Register #(.width(32)) register_5 (.D(WriteData0), .en(1'b1), .clk(clk), .Q(WriteDataStage5));  // open: clr
  Register #(.width(46)) register_6 (.D(ExInstStage4), .en(1'b1), .clk(clk), .Q(ExInstStage5));  // open: clr

  // Other names for the same wires on the sheet: ReadIndex1[4:0] = InstStage2[19:15];
  //   ReadIndex2[4:0] = InstStage2[24:20]; ALUresultStage4[31:0] = MemAddress; WriteIndex[4:0] = ExInstStage5[11:7]

  // Notes on the sheet:
  //   To IMEM
  //   IMEM (do **NOT** move this)
  //   From IMEM
  //   Inputs/Outputs for testing. Do **NOT** move these.
  //   It is OK to move the PC, RegFile, ALU, MEM, Branch Comp, Imm Gen, Partial Load, Partial Store and Control Logic to wherever is most convenient for you when constructing your CPU, and to delete this text
  //   To DMEM
  //   DMEM (do **NOT** move this)
  //   From DMEM
endmodule
