// Logisim project forwarding_control_logic.circ as structural Verilog: 1 circuit, main circuit forwarding_control_logic
module forwarding_control_logic (
  input  [45:0] instALU,
  input  [45:0] instMA,
  input  [45:0] instWB,
  output [1:0] ForwardSelA,
  output [1:0] ForwardSelB,
  output [1:0] ForwardSelSW
);

  wire comparator_1_eq, comparator_2_eq, comparator_3_eq, comparator_4_eq, comparator_5_eq, comparator_6_eq,
       comparator_7_eq, comparator_8_eq, comparator_9_eq, or_1_out, or_2_out;
  wire [1:0] multiplexer_1_out, multiplexer_2_out, multiplexer_3_out, multiplexer_4_out;

  Comparator #(.width(5)) comparator_1 (.a(instALU[19:15]), .b(instWB[11:7]), .eq(comparator_1_eq));  // open: gt, lt
  Multiplexer #(.width(2)) multiplexer_1 (.in0(2'b10), .in1(2'b01), .out(multiplexer_1_out), .sel(comparator_2_eq));
  Comparator #(.width(5)) comparator_2 (.a(instALU[24:20]), .b(instWB[11:7]), .eq(comparator_2_eq));  // open: gt, lt
  Multiplexer #(.width(2)) multiplexer_2 (.in0(2'b10), .in1(2'b01), .out(multiplexer_2_out), .sel(comparator_1_eq));
  Comparator #(.width(5)) comparator_3 (.a(instALU[19:15]), .b(instMA[11:7]), .eq(comparator_3_eq));  // open: gt, lt
  Multiplexer #(.width(2)) multiplexer_3 (
    .in0(multiplexer_1_out), .in1(2'b00), .out(multiplexer_3_out), .sel(comparator_4_eq));
  Comparator #(.width(5)) comparator_4 (.a(instALU[24:20]), .b(instMA[11:7]), .eq(comparator_4_eq));  // open: gt, lt
  Multiplexer #(.width(2)) multiplexer_4 (
    .in0(multiplexer_2_out), .in1(2'b00), .out(multiplexer_4_out), .sel(comparator_3_eq));
  Comparator #(.width(46)) comparator_5 (.a(instALU), .b({46{1'b0}}), .eq(comparator_5_eq));  // open: gt, lt
  Comparator #(.width(46)) comparator_6 (.a(instMA), .b({46{1'b0}}), .eq(comparator_6_eq));  // open: gt, lt
  Comparator #(.width(46)) comparator_7 (.a(instALU), .b({46{1'b0}}), .eq(comparator_7_eq));  // open: gt, lt
  Comparator #(.width(46)) comparator_8 (.a(instMA), .b({46{1'b0}}), .eq(comparator_8_eq));  // open: gt, lt
  or or_1 (or_1_out, comparator_5_eq, comparator_6_eq);
  Multiplexer #(.width(2)) multiplexer_5 (.in0(multiplexer_4_out), .in1(2'b10), .out(ForwardSelA), .sel(or_2_out));
  or or_2 (or_2_out, comparator_7_eq, comparator_8_eq);
  Multiplexer #(.width(2)) multiplexer_6 (.in0(multiplexer_3_out), .in1(2'b10), .out(ForwardSelSW), .sel(or_1_out));
  Comparator #(.width(7)) comparator_9 (.a(instALU[6:0]), .b(7'b0100011), .eq(comparator_9_eq));  // open: gt, lt
  Multiplexer #(.width(2)) multiplexer_7 (.in0(ForwardSelSW), .in1(2'b10), .out(ForwardSelB), .sel(comparator_9_eq));

  // Other names for the same wires on the sheet: ALUsourceA[4:0] = instALU[19:15]; ALUsourceB[4:0] = instALU[24:20];
  //   DestN[4:0] = instMA[11:7]; DestNN[4:0] = instWB[11:7]
endmodule
