// Logisim project partial-store.circ as structural Verilog: 1 circuit, main circuit partial_store
module partial_store (
  input  [31:0] Instruction,
  input  [31:0] MemAddress,
  input  [31:0] DataFromReg,
  input  MemWEn,
  output [3:0] MemWriteMask,
  output [31:0] DataToMem
);

  wire comparator_1_eq;
  wire [1:0] ButtomBits;
  wire [3:0] and_1_out, and_2_out, and_3_out, and_4_out, and_5_out, and_6_out, and_7_out, bit_extender_1_out,
       bit_extender_2_out, bit_extender_3_out, bit_extender_5_out, bit_extender_6_out, bit_extender_7_out,
       bit_extender_8_out, multiplexer_1_out, multiplexer_2_out, multiplexer_4_out;
  wire [6:0] bit_extender_9_out;
  wire [31:0] multiplexer_3_out, multiplexer_5_out;

  assign bit_extender_1_out = {{3{MemWEn}}, MemWEn};  // Bit_Extender bit_extender_1
  assign bit_extender_2_out = {{3{MemWEn}}, MemWEn};  // Bit_Extender bit_extender_2
  assign bit_extender_3_out = {{3{MemWEn}}, MemWEn};  // Bit_Extender bit_extender_3
  Bit_Extender #(.in_width(32), .out_width(2), .\type ("zero")) bit_extender_4 (.in(MemAddress), .out(ButtomBits));
  // Probe on bit_extender_5_out
  assign bit_extender_5_out = {{3{MemWEn}}, MemWEn};  // Bit_Extender bit_extender_5
  assign bit_extender_6_out = {{3{MemWEn}}, MemWEn};  // Bit_Extender bit_extender_6
  assign bit_extender_7_out = {{3{MemWEn}}, MemWEn};  // Bit_Extender bit_extender_7
  assign bit_extender_8_out = {{3{MemWEn}}, MemWEn};  // Bit_Extender bit_extender_8
  assign and_1_out = bit_extender_5_out & 4'b0001;  // AND_Gate and_1, 4 bits wide
  assign and_2_out = bit_extender_6_out & 4'b0010;  // AND_Gate and_2, 4 bits wide
  assign and_3_out = bit_extender_7_out & 4'b0100;  // AND_Gate and_3, 4 bits wide
  assign and_4_out = bit_extender_8_out & 4'b1000;  // AND_Gate and_4, 4 bits wide
  assign and_5_out = bit_extender_1_out & 4'b0011;  // AND_Gate and_5, 4 bits wide
  assign and_6_out = bit_extender_2_out & 4'b1100;  // AND_Gate and_6, 4 bits wide
  assign and_7_out = bit_extender_3_out & 4'b1111;  // AND_Gate and_7, 4 bits wide
  // Probe on and_1_out
  Multiplexer #(.select(2), .width(4)) multiplexer_1 (
    .in0(and_1_out), .in1(and_2_out), .in2(and_3_out), .in3(and_4_out), .out(multiplexer_1_out),
    .sel(ButtomBits));
  Multiplexer #(.select(2), .width(4)) multiplexer_2 (
    .in0(and_5_out), .in2(and_6_out), .out(multiplexer_2_out), .sel(ButtomBits));  // open: in1, in3
  Multiplexer #(.select(2), .width(32)) multiplexer_3 (
    .in0({{16{1'b0}}, DataFromReg[15:0]}), .in2({DataFromReg[15:0], {16{1'b0}}}), .out(multiplexer_3_out),
    .sel(ButtomBits));  // open: in1, in3
  Multiplexer #(.select(3), .width(4)) multiplexer_4 (
    .in0(multiplexer_1_out), .in1(multiplexer_2_out), .in2(and_7_out), .out(multiplexer_4_out),
    .sel(Instruction[14:12]));  // open: in3, in4, in5, in6, in7
  Multiplexer #(.select(2), .width(32)) multiplexer_5 (
    .in0({{24{1'b0}}, DataFromReg[7:0]}), .in1({{16{1'b0}}, DataFromReg[7:0], {8{1'b0}}}),
    .in2({{8{1'b0}}, DataFromReg[7:0], {16{1'b0}}}), .in3({DataFromReg[7:0], {24{1'b0}}}),
    .out(multiplexer_5_out), .sel(ButtomBits));
  Bit_Extender #(.in_width(32), .out_width(7), .\type ("zero")) bit_extender_9 (
    .in(Instruction), .out(bit_extender_9_out));
  Multiplexer #(.select(3), .width(32)) multiplexer_6 (
    .in0(multiplexer_5_out), .in1(multiplexer_3_out), .in2(DataFromReg), .in3(DataFromReg), .out(DataToMem),
    .sel(Instruction[14:12]));  // open: in4, in5, in6, in7
  Comparator #(.width(7)) comparator_1 (.a(bit_extender_9_out), .b(7'b0100011), .eq(comparator_1_eq));  // open: gt, lt
  Multiplexer #(.width(4)) multiplexer_7 (
    .in0(4'b0000), .in1(multiplexer_4_out), .out(MemWriteMask), .sel(comparator_1_eq));

  // Other names for the same wires on the sheet: Func3[2:0] = Instruction[14:12]

  // Notes on the sheet:
  //   INPUTS to your circuit
  //   DON'T CHANGE THE LOCATIONS OF THE INPUTS AND OUTPUTS!
  //   OUTPUT from your circuit
endmodule
