// Logisim project regfile.circ as structural Verilog: 1 circuit, main circuit regfile
module regfile (
  input  [4:0] ReadIndex1,
  input  [4:0] ReadIndex2,
  input  [4:0] WriteIndex,
  input  [31:0] WriteData,
  input  RegWEn,
  input  clk,
  output [31:0] ra,
  output [31:0] sp,
  output [31:0] t0,
  output [31:0] t1,
  output [31:0] t2,
  output [31:0] s0,
  output [31:0] s1,
  output [31:0] a0,
  output [31:0] ReadData1,
  output [31:0] ReadData2
);

  wire d00, d1, d2, d3, d4, d5, d6, d7, d8, d9, d10, d11, d12, d13, d14, d15, d16, d17, d18, d19, d20, d21,
       d22, d23, d24, d25, d26, d27, d28, d29, d30, d31, WE0, WE1, WE2, WE3, WE4, WE5, WE6, WE7, WE8, WE9,
       WE10, WE11, WE12, WE13, WE14, WE15, WE16, WE17, WE18, WE19, WE20, WE21, WE22, WE23, WE24, WE25, WE26,
       WE27, WE28, WE29, WE30, WE31;
  wire [31:0] x00, x3, x4, x11, x12, x13, x14, x15, x16, x17, x18, x19, x20, x21, x22, x23, x24, x25, x26,
       x27, x28, x29, x30, x31;

  Register #(.width(32)) x0 (.D({32{1'b0}}), .en(WE0), .clk(clk), .Q(x00));  // open: clr
  Register #(.width(32)) register_1 (.D(WriteData), .en(WE1), .clk(clk), .Q(ra));  // open: clr
  Register #(.width(32)) register_2 (.D(WriteData), .en(WE2), .clk(clk), .Q(sp));  // open: clr
  Register #(.width(32)) register_3 (.D(WriteData), .en(WE3), .clk(clk), .Q(x3));  // open: clr
  Register #(.width(32)) register_4 (.D(WriteData), .en(WE4), .clk(clk), .Q(x4));  // open: clr
  Register #(.width(32)) register_5 (.D(WriteData), .en(WE5), .clk(clk), .Q(t0));  // open: clr
  Register #(.width(32)) register_6 (.D(WriteData), .en(WE6), .clk(clk), .Q(t1));  // open: clr
  Register #(.width(32)) register_7 (.D(WriteData), .en(WE7), .clk(clk), .Q(t2));  // open: clr
  Register #(.width(32)) register_8 (.D(WriteData), .en(WE8), .clk(clk), .Q(s0));  // open: clr
  Register #(.width(32)) register_9 (.D(WriteData), .en(WE9), .clk(clk), .Q(s1));  // open: clr
  Register #(.width(32)) register_10 (.D(WriteData), .en(WE10), .clk(clk), .Q(a0));  // open: clr
  Register #(.width(32)) register_11 (.D(WriteData), .en(WE11), .clk(clk), .Q(x11));  // open: clr
  Register #(.width(32)) register_12 (.D(WriteData), .en(WE12), .clk(clk), .Q(x12));  // open: clr
  Register #(.width(32)) register_13 (.D(WriteData), .en(WE13), .clk(clk), .Q(x13));  // open: clr
  Register #(.width(32)) register_14 (.D(WriteData), .en(WE14), .clk(clk), .Q(x14));  // open: clr
  Register #(.width(32)) register_15 (.D(WriteData), .en(WE15), .clk(clk), .Q(x15));  // open: clr
  Register #(.width(32)) register_16 (.D(WriteData), .en(WE16), .clk(clk), .Q(x16));  // open: clr
  Register #(.width(32)) register_17 (.D(WriteData), .en(WE17), .clk(clk), .Q(x17));  // open: clr
  Register #(.width(32)) register_18 (.D(WriteData), .en(WE18), .clk(clk), .Q(x18));  // open: clr
  Register #(.width(32)) register_19 (.D(WriteData), .en(WE19), .clk(clk), .Q(x19));  // open: clr
  Register #(.width(32)) register_20 (.D(WriteData), .en(WE20), .clk(clk), .Q(x20));  // open: clr
  Register #(.width(32)) register_21 (.D(WriteData), .en(WE21), .clk(clk), .Q(x21));  // open: clr
  Register #(.width(32)) register_22 (.D(WriteData), .en(WE22), .clk(clk), .Q(x22));  // open: clr
  Register #(.width(32)) register_23 (.D(WriteData), .en(WE23), .clk(clk), .Q(x23));  // open: clr
  Register #(.width(32)) register_24 (.D(WriteData), .en(WE24), .clk(clk), .Q(x24));  // open: clr
  Register #(.width(32)) register_25 (.D(WriteData), .en(WE25), .clk(clk), .Q(x25));  // open: clr
  Register #(.width(32)) register_26 (.D(WriteData), .en(WE26), .clk(clk), .Q(x26));  // open: clr
  Register #(.width(32)) register_27 (.D(WriteData), .en(WE27), .clk(clk), .Q(x27));  // open: clr
  Register #(.width(32)) register_28 (.D(WriteData), .en(WE28), .clk(clk), .Q(x28));  // open: clr
  Register #(.width(32)) register_29 (.D(WriteData), .en(WE29), .clk(clk), .Q(x29));  // open: clr
  Register #(.width(32)) register_30 (.D(WriteData), .en(WE30), .clk(clk), .Q(x30));  // open: clr
  Register #(.width(32)) register_31 (.D(WriteData), .en(WE31), .clk(clk), .Q(x31));  // open: clr
  Multiplexer #(.select(5), .width(32)) multiplexer_1 (
    .in0(x00), .in1(ra), .in2(sp), .in3(x3), .in4(x4), .in5(t0), .in6(t1), .in7(t2), .in8(s0), .in9(s1),
    .in10(a0), .in11(x11), .in12(x12), .in13(x13), .in14(x14), .in15(x15), .in16(x16), .in17(x17),
    .in18(x18), .in19(x19), .in20(x20), .in21(x21), .in22(x22), .in23(x23), .in24(x24), .in25(x25),
    .in26(x26), .in27(x27), .in28(x28), .in29(x29), .in30(x30), .in31(x31), .out(ReadData1), .sel(ReadIndex1));
  Multiplexer #(.select(5), .width(32)) multiplexer_2 (
    .in0(x00), .in1(ra), .in2(sp), .in3(x3), .in4(x4), .in5(t0), .in6(t1), .in7(t2), .in8(s0), .in9(s1),
    .in10(a0), .in11(x11), .in12(x12), .in13(x13), .in14(x14), .in15(x15), .in16(x16), .in17(x17),
    .in18(x18), .in19(x19), .in20(x20), .in21(x21), .in22(x22), .in23(x23), .in24(x24), .in25(x25),
    .in26(x26), .in27(x27), .in28(x28), .in29(x29), .in30(x30), .in31(x31), .out(ReadData2), .sel(ReadIndex2));
  Decoder #(.select(5)) decoder_1 (
    .out0(d00), .out1(d1), .out2(d2), .out3(d3), .out4(d4), .out5(d5), .out6(d6), .out7(d7), .out8(d8),
    .out9(d9), .out10(d10), .out11(d11), .out12(d12), .out13(d13), .out14(d14), .out15(d15), .out16(d16),
    .out17(d17), .out18(d18), .out19(d19), .out20(d20), .out21(d21), .out22(d22), .out23(d23), .out24(d24),
    .out25(d25), .out26(d26), .out27(d27), .out28(d28), .out29(d29), .out30(d30), .out31(d31),
    .sel(WriteIndex));  // open: en
  and and_1 (WE10, RegWEn, d10);
  and and_2 (WE11, RegWEn, d11);
  and and_3 (WE12, RegWEn, d12);
  and and_4 (WE13, RegWEn, d13);
  and and_5 (WE14, RegWEn, d14);
  and and_6 (WE15, RegWEn, d15);
  and and_7 (WE16, RegWEn, d16);
  and and_8 (WE17, RegWEn, d17);
  and and_9 (WE18, RegWEn, d18);
  and and_10 (WE19, RegWEn, d19);
  and and_11 (WE20, RegWEn, d20);
  and and_12 (WE21, RegWEn, d21);
  and and_13 (WE22, RegWEn, d22);
  and and_14 (WE23, RegWEn, d23);
  and and_15 (WE24, RegWEn, d24);
  and and_16 (WE25, RegWEn, d25);
  and and_17 (WE26, RegWEn, d26);
  and and_18 (WE27, RegWEn, d27);
  and and_19 (WE28, RegWEn, d28);
  and and_20 (WE29, RegWEn, d29);
  and and_21 (WE30, RegWEn, d30);
  and and_22 (WE31, RegWEn, d31);
  and and_23 (WE0, RegWEn, d00);
  and and_24 (WE1, RegWEn, d1);
  and and_25 (WE2, RegWEn, d2);
  and and_26 (WE3, RegWEn, d3);
  and and_27 (WE4, RegWEn, d4);
  and and_28 (WE5, RegWEn, d5);
  and and_29 (WE6, RegWEn, d6);
  and and_30 (WE7, RegWEn, d7);
  and and_31 (WE8, RegWEn, d8);
  and and_32 (WE9, RegWEn, d9);

  // Other names for the same wires on the sheet: ReadData01[31:0] = ReadData1; ReadData02[31:0] = ReadData2;
  //   x1[31:0] = ra; x2[31:0] = sp; x5[31:0] = t0; x6[31:0] = t1; x7[31:0] = t2; x8[31:0] = s0; x9[31:0] = s1;
  //   x10[31:0] = a0

  // Notes on the sheet:
  //   INPUTS to your circuit
  //   DON'T CHANGE THE LOCATIONS OF THE INPUTS AND OUTPUTS!
  //   These are DEBUG/TEST outputs from your circuit.
  //   OUTPUTS from your circuit
endmodule
